// Logisim project control-logic.circ as structural Verilog: 10 circuits, main circuit control_logic
module control_logic (
  input  [31:0] inst,
  input  BrEq,
  input  BrLt,
  output PCSel,
  output RegWEn,
  output [2:0] ImmSel,
  output BrUn,
  output ASel,
  output BSel,
  output [3:0] ALUSel,
  output MemRW,
  output [1:0] WBSel,
  output CSRSel,
  output CSRWen,
  output [5:0] out_15
);

  wire and_1_out, PCJa, PCSelCMP, PCSelOp;

  ROM #(.addrWidth(6), .dataWidth(16)) rom_1 (
    .addr(out_15), .data({RegWEn, ImmSel, BrUn, ASel, BSel, ALUSel, MemRW, WBSel, CSRSel, CSRWen}));
  bit0 bit0_1 (.a(inst[6:2]), .b(inst[14:12]), .c({inst[30], inst[25]}), .F(out_15[0]));
  bit1 bit1_1 (.opcode(inst[6:2]), .Funct3(inst[14:12]), .Funct7({inst[30], inst[25]}), .B1(out_15[1]));
  bit2 bit2_1 (.opcode({inst[6:4], inst[2]}), .Funct3(inst[14:12]), .Funct7({inst[30], inst[25]}), .B2(out_15[2]));
  bit3 bit3_1 (.opcode({inst[6:4], inst[2]}), .Funct3(inst[14:12]), .Funct7({inst[30], inst[25]}), .B3(out_15[3]));
  bit4 bit4_1 (.opcode({inst[6:4], inst[2]}), .Funct3(inst[14:12]), .Funct7({inst[30], inst[25]}), .B4(out_15[4]));
  pc_ja pc_ja_1 (.opcode(inst[6:2]), .pc_sel_op(PCJa));
  pc_sel_opcode pc_sel_opcode_1 (.opcode(inst[6:2]), .B5(PCSelOp));
  bit5 bit5_1 (.opcode(inst[6:2]), .Funct3(inst[14:12]), .B5(out_15[5]));
  and and_1 (and_1_out, PCSelOp, PCSelCMP);
  or or_1 (PCSel, and_1_out, PCJa);
  pc_sel_cmp pc_sel_cmp_1 (.Funct3(inst[14:12]), .BRC({BrEq, BrLt}), .SEL(PCSelCMP));

  // Other names for the same wires on the sheet: Funct3[2:0] = inst[14:12]; rom_input[5:0] = out_15

  // Notes on the sheet:
  //   INPUTS to your circuit
  //   Connect ROM Input here ->
  //   contents of rom_1 (hex, n*v repeats v):
  //   8604 8704 8784 8624 8724 8764 8644 8684 86a4 87a4 86c4 86e4 8400 8400 8400 8404 8424 8444 8484 84a4
  //   85a4 84c4 84e4 1410 1410 1410 4*2000 2800 2800 b004 b00c c008 8408 d001 d003
  //   ROM FOR CONTROL LOGIC
  //   DON'T CHANGE THE LOCATIONS OF THE INPUTS AND OUTPUTS!
  //   OUTPUT from your circuit
  //   CLOSE
  //   WIRE
  //   TO
  //   USE
  //   ROM
  //   Reminder: Use combinational logic for PCSel
endmodule

module bit0 (
  input  [4:0] a,
  input  [2:0] b,
  input  [1:0] c,
  output F
);

  wire and_1_out, and_2_out, and_3_out, and_4_out, and_5_out, and_6_out, and_7_out, and_8_out, and_9_out,
       and_10_out, and_11_out, and_12_out, and_13_out, and_14_out, and_15_out, and_16_out, not_1_out,
       not_2_out, not_3_out, not_4_out, not_5_out, not_6_out, not_7_out, not_8_out, not_9_out, not_10_out;

  not not_1 (not_1_out, a[4]);
  not not_2 (not_2_out, a[3]);
  not not_3 (not_3_out, a[2]);
  not not_4 (not_4_out, a[1]);
  not not_5 (not_5_out, a[0]);
  not not_6 (not_6_out, b[2]);
  not not_7 (not_7_out, b[1]);
  not not_8 (not_8_out, b[0]);
  not not_9 (not_9_out, c[1]);
  not not_10 (not_10_out, c[0]);
  and and_1 (and_1_out, not_1_out, not_2_out, not_3_out, not_4_out, not_5_out, not_6_out, not_7_out, b[0]);
  and and_2 (and_2_out, not_1_out, not_2_out, a[2], not_4_out, not_5_out, not_6_out, not_8_out);
  and and_3 (and_3_out, not_1_out, not_2_out, a[2], not_4_out, not_5_out, b[1], not_8_out);
  and and_4 (and_4_out, not_1_out, not_2_out, a[2], not_4_out, not_5_out, b[2], not_7_out, b[0], not_9_out, not_10_out);
  and and_5 (and_5_out, not_1_out, a[3], not_3_out, not_4_out, not_5_out, not_6_out, not_8_out);
  and and_6 (and_6_out, not_1_out, a[3], not_4_out, not_5_out, not_6_out, not_7_out, not_8_out, not_9_out, c[0]);
  and and_7 (and_7_out, not_1_out, a[3], a[2], not_4_out, not_6_out, not_7_out, b[0], not_9_out, not_10_out);
  and and_8 (and_8_out, not_1_out, a[3], a[2], not_4_out, not_6_out, b[1], b[0], not_9_out, c[0]);
  and and_9 (and_9_out, not_1_out, a[3], a[2], not_4_out, b[2], not_7_out, not_8_out, not_9_out, not_10_out);
  and and_10 (and_10_out, a[3], a[2], not_4_out, not_5_out, b[2], not_7_out, b[0], c[1], not_10_out);
  and and_11 (and_11_out, not_1_out, a[3], a[2], not_4_out, b[2], b[1], b[0], not_9_out, not_10_out);
  and and_12 (and_12_out, not_1_out, a[3], a[2], not_4_out, a[0]);
  and and_13 (and_13_out, a[4], a[3], not_3_out, not_4_out, not_5_out, not_7_out, b[0]);
  and and_14 (and_14_out, a[4], a[3], not_3_out, not_4_out, not_5_out, b[2], b[0]);
  and and_15 (and_15_out, a[4], a[3], not_4_out, not_5_out, b[2], not_7_out, b[0]);
  and and_16 (and_16_out, a[4], a[3], not_3_out, not_4_out, a[0], not_6_out, not_7_out, not_8_out);
  or or_1 (F, and_1_out, and_2_out, and_3_out, and_4_out, and_5_out, and_6_out, and_7_out, and_8_out, and_9_out, and_10_out, and_11_out, and_12_out, and_13_out, and_14_out, and_15_out, and_16_out);
endmodule

module bit1 (
  input  [4:0] opcode,
  input  [2:0] Funct3,
  input  [1:0] Funct7,
  output B1
);

  wire and_1_out, and_2_out, and_3_out, and_4_out, and_5_out, and_6_out, and_7_out, and_8_out, and_9_out,
       and_10_out, and_11_out, and_12_out, and_13_out, and_14_out, not_1_out, not_2_out, not_3_out,
       not_4_out, not_5_out, not_6_out, not_7_out, not_8_out, not_9_out, not_10_out;

  not not_1 (not_1_out, opcode[4]);
  not not_2 (not_2_out, opcode[3]);
  not not_3 (not_3_out, opcode[2]);
  not not_4 (not_4_out, opcode[1]);
  not not_5 (not_5_out, opcode[0]);
  not not_6 (not_6_out, Funct3[2]);
  not not_7 (not_7_out, Funct3[1]);
  not not_8 (not_8_out, Funct3[0]);
  not not_9 (not_9_out, Funct7[1]);
  not not_10 (not_10_out, Funct7[0]);
  and and_1 (and_1_out, not_1_out, not_2_out, not_3_out, not_4_out, not_5_out, not_6_out, Funct3[1], not_8_out);
  and and_2 (and_2_out, not_1_out, not_2_out, opcode[2], not_4_out, not_5_out, not_7_out, not_8_out);
  and and_3 (and_3_out, not_1_out, not_2_out, opcode[2], not_4_out, not_5_out, Funct3[2], not_7_out, not_9_out, not_10_out);
  and and_4 (and_4_out, not_1_out, opcode[2], not_4_out, not_5_out, Funct3[2], not_7_out, not_8_out, not_9_out, not_10_out);
  and and_5 (and_5_out, not_1_out, not_2_out, opcode[2], not_4_out, not_5_out, Funct3[2], Funct3[1], Funct3[0]);
  and and_6 (and_6_out, opcode[3], not_3_out, not_4_out, not_5_out, not_6_out, not_7_out, not_8_out);
  and and_7 (and_7_out, not_1_out, opcode[3], not_4_out, not_5_out, not_6_out, not_7_out, not_8_out, Funct7[1], not_10_out);
  and and_8 (and_8_out, not_1_out, opcode[3], opcode[2], not_4_out, not_5_out, not_6_out, not_7_out, Funct3[0], not_9_out, not_10_out);
  and and_9 (and_9_out, not_1_out, opcode[3], opcode[2], not_4_out, not_5_out, Funct3[1], not_8_out, not_9_out, not_10_out);
  and and_10 (and_10_out, not_1_out, opcode[3], opcode[2], not_4_out, not_5_out, Funct3[2], Funct3[1], not_9_out, not_10_out);
  and and_11 (and_11_out, opcode[4], opcode[3], not_3_out, not_4_out, not_5_out, not_6_out, not_7_out);
  and and_12 (and_12_out, opcode[4], opcode[3], not_3_out, not_4_out, not_6_out, not_7_out, not_8_out);
  and and_13 (and_13_out, opcode[4], opcode[3], not_3_out, not_4_out, not_5_out, Funct3[2], Funct3[1]);
  and and_14 (and_14_out, opcode[4], opcode[3], not_3_out, opcode[1], opcode[0]);
  or or_1 (B1, and_1_out, and_2_out, and_3_out, and_4_out, and_5_out, and_6_out, and_7_out, and_8_out, and_9_out, and_10_out, and_11_out, and_12_out, and_13_out, and_14_out);
endmodule

module bit2 (
  input  [3:0] opcode,
  input  [2:0] Funct3,
  input  [1:0] Funct7,
  output B2
);

  wire and_1_out, and_2_out, and_3_out, and_4_out, and_5_out, and_6_out, and_7_out, and_8_out, and_9_out,
       and_10_out, and_11_out, not_1_out, not_2_out, not_3_out, not_4_out, not_5_out, not_6_out, not_7_out,
       not_8_out, not_9_out;

  not not_1 (not_1_out, opcode[3]);
  not not_2 (not_2_out, opcode[2]);
  not not_3 (not_3_out, opcode[1]);
  not not_4 (not_4_out, opcode[0]);
  not not_5 (not_5_out, Funct3[2]);
  not not_6 (not_6_out, Funct3[1]);
  not not_7 (not_7_out, Funct3[0]);
  not not_8 (not_8_out, Funct7[1]);
  not not_9 (not_9_out, Funct7[0]);
  and and_1 (and_1_out, not_1_out, not_2_out, not_3_out, not_4_out, not_5_out, not_6_out);
  and and_2 (and_2_out, not_1_out, not_2_out, not_3_out, not_4_out, not_5_out, not_7_out);
  and and_3 (and_3_out, not_1_out, not_2_out, not_4_out, not_5_out, not_6_out, not_7_out);
  and and_4 (and_4_out, not_1_out, not_3_out, not_4_out, not_5_out, not_6_out, not_7_out);
  and and_5 (and_5_out, not_1_out, not_2_out, opcode[1], not_4_out, Funct3[2], Funct3[0], Funct7[1], not_9_out);
  and and_6 (and_6_out, not_1_out, not_2_out, opcode[1], not_4_out, Funct3[2], Funct3[1]);
  and and_7 (and_7_out, not_1_out, opcode[2], opcode[1], not_4_out, not_5_out, Funct3[0], not_8_out, Funct7[0]);
  and and_8 (and_8_out, not_1_out, opcode[2], opcode[1], not_4_out, not_5_out, Funct3[1], not_7_out, not_8_out, not_9_out);
  and and_9 (and_9_out, not_1_out, opcode[2], opcode[1], not_4_out, Funct3[2], not_6_out, not_7_out, not_8_out, not_9_out);
  and and_10 (and_10_out, opcode[3], opcode[2], not_3_out, not_4_out, Funct3[2]);
  and and_11 (and_11_out, opcode[3], opcode[2], opcode[1], not_4_out, not_6_out, Funct3[0]);
  or or_1 (B2, and_1_out, and_2_out, and_3_out, and_4_out, and_5_out, and_6_out, and_7_out, and_8_out, and_9_out, and_10_out, and_11_out);
endmodule

module bit3 (
  input  [3:0] opcode,
  input  [2:0] Funct3,
  input  [1:0] Funct7,
  output B3
);

  wire and_1_out, and_2_out, and_3_out, and_4_out, and_5_out, and_6_out, and_7_out, not_1_out, not_2_out,
       not_3_out, not_4_out, not_5_out, not_6_out, not_7_out, not_8_out, not_9_out;

  not not_1 (not_1_out, opcode[3]);
  not not_2 (not_2_out, opcode[2]);
  not not_3 (not_3_out, opcode[1]);
  not not_4 (not_4_out, opcode[0]);
  not not_5 (not_5_out, Funct3[2]);
  not not_6 (not_6_out, Funct3[1]);
  not not_7 (not_7_out, Funct3[0]);
  not not_8 (not_8_out, Funct7[1]);
  not not_9 (not_9_out, Funct7[0]);
  and and_1 (and_1_out, not_1_out, not_2_out, not_4_out, not_5_out, not_6_out, not_7_out);
  and and_2 (and_2_out, not_1_out, not_3_out, not_4_out, not_5_out, not_6_out, Funct3[0]);
  and and_3 (and_3_out, not_1_out, not_3_out, not_4_out, not_5_out, Funct3[1], not_7_out);
  and and_4 (and_4_out, not_1_out, opcode[2], opcode[1], not_4_out, Funct3[2], not_6_out, Funct3[0], not_9_out);
  and and_5 (and_5_out, not_1_out, opcode[2], opcode[1], not_4_out, Funct3[2], Funct3[1], not_8_out, not_9_out);
  and and_6 (and_6_out, opcode[3], opcode[2], not_3_out, not_4_out, not_6_out);
  and and_7 (and_7_out, opcode[3], opcode[2], not_3_out, not_4_out, Funct3[2]);
  or or_1 (B3, and_1_out, and_2_out, and_3_out, and_4_out, and_5_out, and_6_out, and_7_out);
endmodule

module bit4 (
  input  [3:0] opcode,
  input  [2:0] Funct3,
  input  [1:0] Funct7,
  output B4
);

  wire and_1_out, and_2_out, and_3_out, and_4_out, and_5_out, and_6_out, and_7_out, and_8_out, not_1_out,
       not_2_out, not_3_out, not_4_out, not_5_out, not_6_out, not_7_out, not_8_out, not_9_out;

  not not_1 (not_1_out, opcode[3]);
  not not_2 (not_2_out, opcode[2]);
  not not_3 (not_3_out, opcode[1]);
  not not_4 (not_4_out, opcode[0]);
  not not_5 (not_5_out, Funct3[2]);
  not not_6 (not_6_out, Funct3[1]);
  not not_7 (not_7_out, Funct3[0]);
  not not_8 (not_8_out, Funct7[1]);
  not not_9 (not_9_out, Funct7[0]);
  and and_1 (and_1_out, not_1_out, not_2_out, opcode[1], not_4_out, not_6_out, Funct3[0], not_8_out, not_9_out);
  and and_2 (and_2_out, not_1_out, not_2_out, opcode[1], not_4_out, Funct3[1], not_7_out);
  and and_3 (and_3_out, not_1_out, not_2_out, opcode[1], not_4_out, Funct3[2], not_7_out);
  and and_4 (and_4_out, not_1_out, not_2_out, opcode[1], not_4_out, Funct3[2], not_9_out);
  and and_5 (and_5_out, not_1_out, not_2_out, opcode[1], not_4_out, Funct3[2], Funct3[1]);
  and and_6 (and_6_out, not_1_out, opcode[2], not_3_out, not_4_out, not_5_out, not_7_out);
  and and_7 (and_7_out, opcode[2], not_3_out, not_4_out, not_5_out, not_6_out);
  and and_8 (and_8_out, opcode[3], opcode[2], not_3_out, not_4_out, Funct3[2]);
  or or_1 (B4, and_1_out, and_2_out, and_3_out, and_4_out, and_5_out, and_6_out, and_7_out, and_8_out);
endmodule

module bit5 (
  input  [4:0] opcode,
  input  [2:0] Funct3,
  output B5
);

  wire and_1_out, and_2_out, and_3_out, and_4_out, not_1_out, not_2_out, not_3_out, not_4_out, not_5_out,
       not_6_out, not_7_out;

  not not_1 (not_1_out, opcode[4]);
  not not_2 (not_2_out, opcode[2]);
  not not_3 (not_3_out, opcode[1]);
  not not_4 (not_4_out, opcode[0]);
  not not_5 (not_5_out, Funct3[2]);
  not not_6 (not_6_out, Funct3[1]);
  not not_7 (not_7_out, Funct3[0]);
  and and_1 (and_1_out, not_1_out, opcode[2], not_3_out, opcode[0]);
  and and_2 (and_2_out, opcode[4], opcode[3], not_2_out, opcode[0], not_5_out, not_6_out, not_7_out);
  and and_3 (and_3_out, opcode[4], opcode[3], not_2_out, opcode[1], opcode[0]);
  and and_4 (and_4_out, opcode[4], opcode[3], opcode[2], not_3_out, not_4_out, not_6_out, Funct3[0]);
  or or_1 (B5, and_1_out, and_2_out, and_3_out, and_4_out);
endmodule

module pc_sel_opcode (
  input  [4:0] opcode,
  output B5
);

  wire not_1_out, not_2_out, not_3_out;

  not not_1 (not_1_out, opcode[2]);
  not not_2 (not_2_out, opcode[1]);
  not not_3 (not_3_out, opcode[0]);
  and and_1 (B5, opcode[4], opcode[3], not_1_out, not_2_out, not_3_out);
endmodule

module pc_sel_cmp (
  input  [2:0] Funct3,
  input  [1:0] BRC,
  output SEL
);

  wire and_1_out, and_2_out, and_3_out, and_4_out, not_1_out, not_2_out, not_3_out, not_4_out, not_5_out;

  not not_1 (not_1_out, Funct3[2]);
  not not_2 (not_2_out, Funct3[1]);
  not not_3 (not_3_out, Funct3[0]);
  not not_4 (not_4_out, BRC[1]);
  not not_5 (not_5_out, BRC[0]);
  and and_1 (and_1_out, not_1_out, not_2_out, not_3_out, BRC[1]);
  and and_2 (and_2_out, not_1_out, not_2_out, Funct3[0], not_4_out);
  and and_3 (and_3_out, Funct3[2], not_3_out, not_4_out, BRC[0]);
  and and_4 (and_4_out, Funct3[2], Funct3[0], not_5_out);
  or or_1 (SEL, and_1_out, and_2_out, and_3_out, and_4_out);
endmodule

module pc_ja (
  input  [4:0] opcode,
  output pc_sel_op
);

  wire not_1_out;

  not not_1 (not_1_out, opcode[2]);
  and and_1 (pc_sel_op, opcode[4], opcode[3], not_1_out, opcode[0]);
endmodule
