// Logisim project cpu.circ as structural Verilog: 10 circuits, main circuit cpu
module cpu (
  input  clk,
  input  [31:0] INSTRUCTION,
  input  [31:0] MEM_READ_DATA,
  output [31:0] MEM_WRITE_ADDRESS,
  output [31:0] PROGRAM_COUNTER,
  output [31:0] ra,
  output [31:0] sp,
  output [31:0] t0,
  output [31:0] t1,
  output [31:0] t2,
  output [31:0] s0,
  output [31:0] s1,
  output [31:0] a0,
  output [31:0] tohost,
  output [3:0] MEM_WRITE_ENABLE,
  output [31:0] MEM_WRITE_DATA
);

  wire ASel, BrEq, BrLt, BrUn, BSel, control_logic_1_csrsel, CSRWen, MemRW, PCSel, RegWEn;
  wire [1:0] addr_0_1, WBSel;
  wire [2:0] ImmSel;
  wire [3:0] ALUSel, write_en_gen_1_write_en;
  wire [31:0] IMM, multiplexer_1_out, multiplexer_3_out, multiplexer_4_out, multiplexer_5_out, PC_Add_4, rd1,
       rd2, read_data, write_data;

  Adder #(.width(32)) adder_1 (.a(PROGRAM_COUNTER), .b(32'h4), .out(PC_Add_4));  // open: cin, cout
  Register #(.width(32)) PC (.D(multiplexer_1_out), .clk(clk), .Q(PROGRAM_COUNTER));  // open: en, clr
  Multiplexer #(.enable("false"), .width(32)) multiplexer_1 (
    .in0(PC_Add_4), .in1({MEM_WRITE_ADDRESS[31:2], addr_0_1}), .out(multiplexer_1_out), .sel(PCSel));
  Multiplexer #(.enable("false"), .select(2), .width(32)) multiplexer_2 (
    .in0(read_data), .in1({MEM_WRITE_ADDRESS[31:2], addr_0_1}), .in2(PC_Add_4), .in3(IMM), .out(write_data),
    .sel(WBSel));
  imm_gen imm_gen_1 (.inst(INSTRUCTION), .ImmSel(ImmSel), .imm(IMM));
  control_logic control_logic_1 (
    .CSRWen(CSRWen), .PCSel(PCSel), .RegWEn(RegWEn), .ImmSel(ImmSel), .BrUn(BrUn), .ASel(ASel), .BSel(BSel),
    .ALUSel(ALUSel), .MemRW(MemRW), .WBSel(WBSel), .CSRSel(control_logic_1_csrsel), .inst(INSTRUCTION),
    .BrEq(BrEq), .BrLt(BrLt));  // open: out_15
  regfile regfile_1 (
    .rs1(INSTRUCTION[19:15]), .rs2(INSTRUCTION[24:20]), .rd(INSTRUCTION[11:7]), .Write_Data(write_data),
    .RegWEn(RegWEn), .clk(clk), .ra(ra), .sp(sp), .t0(t0), .t1(t1), .t2(t2), .s0(s0), .s1(s1), .a0(a0),
    .Read_Data_1(rd1), .Read_Data_2(rd2));
  branch_comp branch_comp_1 (.rs1(rd1), .rs2(rd2), .BrUn(BrUn), .BrEq(BrEq), .BrLt(BrLt));
  Multiplexer #(.enable("false"), .width(32)) multiplexer_3 (
    .in0(rd1), .in1(IMM), .out(multiplexer_3_out), .sel(control_logic_1_csrsel));
  Multiplexer #(.enable("false"), .width(32)) multiplexer_4 (
    .in0(PROGRAM_COUNTER), .in1(rd1), .out(multiplexer_4_out), .sel(ASel));
  Multiplexer #(.enable("false"), .width(32)) multiplexer_5 (.in0(IMM), .in1(rd2), .out(multiplexer_5_out), .sel(BSel));
  // csr csr_1: pin names not known; wires that end beside it: INSTRUCTION[31:20], multiplexer_3_out, CSRWen, clk, tohost
  alu alu_1 (
    .Result({MEM_WRITE_ADDRESS[31:2], addr_0_1}), .A(multiplexer_4_out), .B(multiplexer_5_out),
    .ALUSel(ALUSel));
  write_en_gen write_en_gen_1 (.Funct3(INSTRUCTION[14:12]), .addr_0_1(addr_0_1), .Write_En(write_en_gen_1_write_en));
  write_sel write_sel_1 (
    .Funct3(INSTRUCTION[14:12]), .addr_0_1(addr_0_1), .Write_data_in(rd2), .write_data_out(MEM_WRITE_DATA));
  Multiplexer #(.enable("false"), .width(4)) multiplexer_6 (
    .in0(4'b0000), .in1(write_en_gen_1_write_en), .out(MEM_WRITE_ENABLE), .sel(MemRW));
  load_sel load_sel_1 (
    .mem_read_data(MEM_READ_DATA), .Funct3(INSTRUCTION[14:12]), .addr_0_1(addr_0_1), .read_data(read_data));

  assign MEM_WRITE_ADDRESS[1:0] = 2'b00;

  // Other names for the same wires on the sheet: ALU_result[31:0] = {MEM_WRITE_ADDRESS[31:2], addr_0_1};
  //   rd[4:0] = INSTRUCTION[11:7]; Funct3[2:0] = INSTRUCTION[14:12]; rs1[4:0] = INSTRUCTION[19:15];
  //   CSR_addr[11:0] = INSTRUCTION[31:20]; rs2[4:0] = INSTRUCTION[24:20]

  // Notes on the sheet:
  //   Output to IMEM
  //   IMEM (do **NOT** move this)
  //   Inputs from IMEM
  //   It is OK to move the PC, RegFile, ALU, MEM, Branch Comp, Imm Gen, and Control Logic to wherever is most convenient for you when constructing your CPU, and to delete this text
  //   Inputs/Outputs for testing. Do **NOT** move these.
  //   Truncate the lower two bit 
  //   Outputs To DMEM
  //   DMEM (do **NOT** move this)
  //   Inputs From DMEM
endmodule

module load_sel_0 (
  input  [2:0] Funct3,
  input  [1:0] addr,
  output bit0
);

  wire and_1_out, and_2_out, not_1_out, not_2_out, not_3_out, not_4_out;

  not not_1 (not_1_out, Funct3[2]);
  not not_2 (not_2_out, Funct3[1]);
  not not_3 (not_3_out, Funct3[0]);
  not not_4 (not_4_out, addr[0]);
  and and_1 (and_1_out, not_1_out, not_2_out, not_3_out, addr[0]);
  and and_2 (and_2_out, not_1_out, not_2_out, Funct3[0], addr[1], not_4_out);
  or or_1 (bit0, and_1_out, and_2_out);
endmodule

module load_sel_1 (
  input  [2:0] Funct3,
  input  [1:0] addr,
  output bit1
);

  wire and_1_out, and_2_out, not_1_out, not_2_out;

  not not_1 (not_1_out, Funct3[2]);
  not not_2 (not_2_out, Funct3[0]);
  and and_1 (and_1_out, not_1_out, not_2_out, addr[1]);
  and and_2 (and_2_out, not_1_out, Funct3[1], not_2_out);
  or or_1 (bit1, and_1_out, and_2_out);
endmodule

module load_sel_2 (
  input  [2:0] Funct3,
  input  [1:0] addr,
  output bit2
);

  wire and_1_out, and_2_out, not_1_out, not_2_out, not_3_out, not_4_out;

  not not_1 (not_1_out, Funct3[2]);
  not not_2 (not_2_out, Funct3[1]);
  not not_3 (not_3_out, Funct3[0]);
  not not_4 (not_4_out, addr[0]);
  and and_1 (and_1_out, not_1_out, not_2_out, Funct3[0], not_4_out);
  and and_2 (and_2_out, not_1_out, Funct3[1], not_3_out);
  or or_1 (bit2, and_1_out, and_2_out);
endmodule

module load_sel (
  input  [31:0] mem_read_data,
  input  [2:0] Funct3,
  input  [1:0] addr_0_1,
  output [31:0] read_data
);

  wire [2:0] load_sel;
  wire [7:0] multiplexer_1_out;
  wire [15:0] multiplexer_2_out;
  wire [31:0] bit_extender_1_out, bit_extender_2_out;

  Multiplexer #(.enable("false"), .select(3), .width(8)) multiplexer_1 (
    .in0(mem_read_data[7:0]), .in1(mem_read_data[15:8]), .in2(mem_read_data[23:16]),
    .in3(mem_read_data[31:24]), .out(multiplexer_1_out), .sel(load_sel));  // open: in4, in5, in6, in7
  Multiplexer #(.enable("false"), .select(3), .width(16)) multiplexer_2 (
    .in4(mem_read_data[15:0]), .in5(mem_read_data[31:16]), .out(multiplexer_2_out), .sel(load_sel));  // open: in0, in1, in2, in3, in6, in7
  assign bit_extender_1_out = {{24{multiplexer_1_out[7]}}, multiplexer_1_out};  // Bit_Extender bit_extender_1
  assign bit_extender_2_out = {{16{multiplexer_2_out[15]}}, multiplexer_2_out};  // Bit_Extender bit_extender_2
  load_sel_0 load_sel_0_1 (.Funct3(Funct3), .addr(addr_0_1), .bit0(load_sel[0]));
  load_sel_1 load_sel_1_1 (.Funct3(Funct3), .addr(addr_0_1), .bit1(load_sel[1]));
  load_sel_2 load_sel_2_1 (.Funct3(Funct3), .addr(addr_0_1), .bit2(load_sel[2]));
  Multiplexer #(.enable("false"), .select(3), .width(32)) multiplexer_3 (
    .in0(bit_extender_1_out), .in1(bit_extender_1_out), .in2(bit_extender_1_out), .in3(bit_extender_1_out),
    .in4(bit_extender_2_out), .in5(bit_extender_2_out), .in6(mem_read_data), .in7(mem_read_data),
    .out(read_data), .sel(load_sel));

  // Other names for the same wires on the sheet: data[31:0] = mem_read_data
endmodule

module write_en_gen (
  input  [2:0] Funct3,
  input  [1:0] addr_0_1,
  output [3:0] Write_En
);

  wire [2:0] write_en_sb0_1_bit0;

  write_en_sb0 write_en_sb0_1 (.Funct3(Funct3), .addr(addr_0_1), .bit0(write_en_sb0_1_bit0[0]));
  write_en_sb1 write_en_sb1_1 (.Funct3(Funct3), .addr(addr_0_1), .bit1(write_en_sb0_1_bit0[1]));
  write_en_sb2 write_en_sb2_1 (.Funct3(Funct3), .addr(addr_0_1), .bit2(write_en_sb0_1_bit0[2]));
  ROM #(.addrWidth(3), .dataWidth(4)) rom_1 (.addr(write_en_sb0_1_bit0), .data(Write_En));

  // Notes on the sheet:
  //   contents of rom_1 (hex, n*v repeats v):
  //   1 2 4 8 3 c f
endmodule

module write_en_sb0 (
  input  [2:0] Funct3,
  input  [1:0] addr,
  output bit0
);

  wire and_1_out, and_2_out, not_1_out, not_2_out, not_3_out, not_4_out;

  not not_1 (not_1_out, Funct3[2]);
  not not_2 (not_2_out, Funct3[1]);
  not not_3 (not_3_out, Funct3[0]);
  not not_4 (not_4_out, addr[0]);
  and and_1 (and_1_out, not_1_out, not_2_out, not_3_out, addr[0]);
  and and_2 (and_2_out, not_1_out, not_2_out, Funct3[0], addr[1], not_4_out);
  or or_1 (bit0, and_1_out, and_2_out);
endmodule

module write_en_sb1 (
  input  [2:0] Funct3,
  input  [1:0] addr,
  output bit1
);

  wire and_1_out, and_2_out, not_1_out, not_2_out;

  not not_1 (not_1_out, Funct3[2]);
  not not_2 (not_2_out, Funct3[0]);
  and and_1 (and_1_out, not_1_out, not_2_out, addr[1]);
  and and_2 (and_2_out, not_1_out, Funct3[1], not_2_out);
  or or_1 (bit1, and_1_out, and_2_out);
endmodule

module write_en_sb2 (
  input  [2:0] Funct3,
  input  [1:0] addr,
  output bit2
);

  wire and_1_out, and_2_out, not_1_out, not_2_out, not_3_out, not_4_out;

  not not_1 (not_1_out, Funct3[2]);
  not not_2 (not_2_out, Funct3[1]);
  not not_3 (not_3_out, Funct3[0]);
  not not_4 (not_4_out, addr[0]);
  and and_1 (and_1_out, not_1_out, not_2_out, Funct3[0], not_4_out);
  and and_2 (and_2_out, not_1_out, Funct3[1], not_3_out);
  or or_1 (bit2, and_1_out, and_2_out);
endmodule

module write_sel (
  input  [2:0] Funct3,
  input  [1:0] addr_0_1,
  input  [31:0] Write_data_in,
  output [31:0] write_data_out
);

  wire [31:0] multiplexer_1_out, multiplexer_2_out;

  Multiplexer #(.enable("false"), .select(2), .width(32)) multiplexer_1 (
    .in0({{24{1'b0}}, Write_data_in[7:0]}), .in1({{16{1'b0}}, Write_data_in[7:0], {8{1'b0}}}),
    .in2({{8{1'b0}}, Write_data_in[7:0], {16{1'b0}}}), .in3({Write_data_in[7:0], {24{1'b0}}}),
    .out(multiplexer_1_out), .sel(addr_0_1));
  Multiplexer #(.enable("false"), .width(32)) multiplexer_2 (
    .in0({{16{1'b0}}, Write_data_in[15:0]}), .in1({Write_data_in[15:0], {16{1'b0}}}),
    .out(multiplexer_2_out), .sel(addr_0_1[1]));
  Multiplexer #(.enable("false"), .select(2), .width(32)) multiplexer_3 (
    .in0(multiplexer_1_out), .in1(multiplexer_2_out), .in2(Write_data_in), .out(write_data_out),
    .sel(Funct3[1:0]));  // open: in3
endmodule
